# Fritzing sketch Power Supply (saved by Fritzing 1.0.1rc)
circuit board: 8.04934cm x 10.8992cm
breadboards: 1

parts:
  M1 = RioRand LM2596
  M2 = RioRand LM2596
  M3 = RioRand LM2596
  C1 = Capacitor [package=cap-pth-small-kit]
  C2 = Capacitor [package=cap-pth-small-kit]
  C3 = Capacitor [package=cap-pth-small-kit]
  C4 = Capacitor [package=cap-pth-small-kit]
  C5 = Capacitor [package=cap-pth-small-kit]
  C6 = Capacitor [package=cap-pth-small-kit]
  C7 = Capacitor [package=cap-pth-small-kit]
  C8 = Capacitor [package=cap-pth-small-kit]
  C9 = Capacitor [package=cap-pth-small-kit]
  Vin_GND = Screw terminal - 2 pins [package=THT]
  Line_Vout_GND = Screw terminal - 2 pins [package=THT]
  5v_-_1A = Screw terminal - 2 pins [package=THT]
  5v_-_750mA = Screw terminal - 2 pins [package=THT]
  J1 = Screw terminal - 2 pins [package=THT]

nets:
  N1: M1.Pin_1, M2.Pin_1, M3.Pin_1, C1.1, C2.1, C3.1, C4.2, C5.2, C6.2, Vin_GND.pin2, Line_Vout_GND.pin1
  N2: M1.Pin_2, M2.Pin_2, M3.Pin_2, C1.2, C2.2, C3.2, C4.1, C5.1, C6.1, Vin_GND.pin1, Line_Vout_GND.pin2
  N3: M1.Pin_3, C7.1, J1.pin2
  N4: M1.Pin_4, C7.2, J1.pin1
  N5: M2.Pin_3, C8.1, 5v_-_750mA.pin2
  N6: M2.Pin_4, C8.2, 5v_-_750mA.pin1
  N7: M3.Pin_3, C9.1, 5v_-_1A.pin2
  N8: M3.Pin_4, C9.2, 5v_-_1A.pin1

notes:
  LM2596 - 5v - 1A
  LM2596 - 5v - 750mA
  LM2596 - 3.3v - 250mA
  v0.0.5
  Made for TAFY
